// Logisim project finished_project.circ as structural Verilog: 1 circuit, main circuit main
// O
module main (
);

  wire and_1_out, and_2_out, and_4_out, and_5_out, and_6_out, and_8_out, button_1_out, clock_1_out,
       comparator_1_eq, comparator_2_gt, decoder_1_out0, decoder_1_out1, decoder_1_out2, decoder_1_out3,
       decoder_1_out4, decoder_1_out5, decoder_1_out6, decoder_1_out7, L_out, not_1_out, not_2_out, or_1_out,
       or_10_out, or_11_out, or_12_out, R_out;
  wire [2:0] counter_1_q, random_1_out;
  wire [3:0] counter_2_q, counter_3_q, counter_4_q, counter_5_q, shift_register_9_q0, shift_register_9_q1,
       shift_register_9_q2, shift_register_9_q3;
  wire [7:0] decoder_2_out0, or_2_out, shift_register_1_q7, shift_register_2_q7, shift_register_3_q7,
       shift_register_4_q7, shift_register_5_q7, shift_register_6_q7, shift_register_7_q7,
       shift_register_8_q7;

  Clock clock_1 (.out(clock_1_out));
  and and_1 (and_1_out, clock_1_out, not_1_out);
  not not_1 (not_1_out, comparator_1_eq);
  Random #(.width(3)) random_1 (.clk(and_1_out), .out(random_1_out));  // open: next, clr
  Decoder #(.select(3)) decoder_1 (
    .out0(decoder_1_out0), .out1(decoder_1_out1), .out2(decoder_1_out2), .out3(decoder_1_out3),
    .out4(decoder_1_out4), .out5(decoder_1_out5), .out6(decoder_1_out6), .out7(decoder_1_out7),
    .sel(random_1_out));  // open: en
  Shift_Register shift_register_1 (
    .clk(and_1_out), .load(and_1_out), .clr(button_1_out), .d0(decoder_1_out0), .q0(shift_register_1_q7[7]),
    .d1(decoder_1_out1), .q1(shift_register_1_q7[6]), .d2(decoder_1_out2), .q2(shift_register_1_q7[5]),
    .d3(decoder_1_out3), .q3(shift_register_1_q7[4]), .d4(decoder_1_out4), .q4(shift_register_1_q7[3]),
    .d5(decoder_1_out5), .q5(shift_register_1_q7[2]), .d6(decoder_1_out6), .q6(shift_register_1_q7[1]),
    .d7(decoder_1_out7), .q7(shift_register_1_q7[0]));  // open: shift, in, out
  Shift_Register shift_register_2 (
    .clk(and_1_out), .load(and_1_out), .clr(button_1_out), .d0(shift_register_1_q7[7]),
    .q0(shift_register_2_q7[7]), .d1(shift_register_1_q7[6]), .q1(shift_register_2_q7[6]),
    .d2(shift_register_1_q7[5]), .q2(shift_register_2_q7[5]), .d3(shift_register_1_q7[4]),
    .q3(shift_register_2_q7[4]), .d4(shift_register_1_q7[3]), .q4(shift_register_2_q7[3]),
    .d5(shift_register_1_q7[2]), .q5(shift_register_2_q7[2]), .d6(shift_register_1_q7[1]),
    .q6(shift_register_2_q7[1]), .d7(shift_register_1_q7[0]), .q7(shift_register_2_q7[0]));  // open: shift, in, out
  Shift_Register shift_register_3 (
    .clk(and_1_out), .load(and_1_out), .clr(button_1_out), .d0(shift_register_2_q7[7]),
    .q0(shift_register_3_q7[7]), .d1(shift_register_2_q7[6]), .q1(shift_register_3_q7[6]),
    .d2(shift_register_2_q7[5]), .q2(shift_register_3_q7[5]), .d3(shift_register_2_q7[4]),
    .q3(shift_register_3_q7[4]), .d4(shift_register_2_q7[3]), .q4(shift_register_3_q7[3]),
    .d5(shift_register_2_q7[2]), .q5(shift_register_3_q7[2]), .d6(shift_register_2_q7[1]),
    .q6(shift_register_3_q7[1]), .d7(shift_register_2_q7[0]), .q7(shift_register_3_q7[0]));  // open: shift, in, out
  Shift_Register shift_register_4 (
    .clk(and_1_out), .load(and_1_out), .clr(button_1_out), .d0(shift_register_3_q7[7]),
    .q0(shift_register_4_q7[7]), .d1(shift_register_3_q7[6]), .q1(shift_register_4_q7[6]),
    .d2(shift_register_3_q7[5]), .q2(shift_register_4_q7[5]), .d3(shift_register_3_q7[4]),
    .q3(shift_register_4_q7[4]), .d4(shift_register_3_q7[3]), .q4(shift_register_4_q7[3]),
    .d5(shift_register_3_q7[2]), .q5(shift_register_4_q7[2]), .d6(shift_register_3_q7[1]),
    .q6(shift_register_4_q7[1]), .d7(shift_register_3_q7[0]), .q7(shift_register_4_q7[0]));  // open: shift, in, out
  Shift_Register shift_register_5 (
    .clk(and_1_out), .load(and_1_out), .clr(button_1_out), .d0(shift_register_4_q7[7]),
    .q0(shift_register_5_q7[7]), .d1(shift_register_4_q7[6]), .q1(shift_register_5_q7[6]),
    .d2(shift_register_4_q7[5]), .q2(shift_register_5_q7[5]), .d3(shift_register_4_q7[4]),
    .q3(shift_register_5_q7[4]), .d4(shift_register_4_q7[3]), .q4(shift_register_5_q7[3]),
    .d5(shift_register_4_q7[2]), .q5(shift_register_5_q7[2]), .d6(shift_register_4_q7[1]),
    .q6(shift_register_5_q7[1]), .d7(shift_register_4_q7[0]), .q7(shift_register_5_q7[0]));  // open: shift, in, out
  Shift_Register shift_register_6 (
    .clk(and_1_out), .load(and_1_out), .clr(button_1_out), .d0(shift_register_5_q7[7]),
    .q0(shift_register_6_q7[7]), .d1(shift_register_5_q7[6]), .q1(shift_register_6_q7[6]),
    .d2(shift_register_5_q7[5]), .q2(shift_register_6_q7[5]), .d3(shift_register_5_q7[4]),
    .q3(shift_register_6_q7[4]), .d4(shift_register_5_q7[3]), .q4(shift_register_6_q7[3]),
    .d5(shift_register_5_q7[2]), .q5(shift_register_6_q7[2]), .d6(shift_register_5_q7[1]),
    .q6(shift_register_6_q7[1]), .d7(shift_register_5_q7[0]), .q7(shift_register_6_q7[0]));  // open: shift, in, out
  Shift_Register shift_register_7 (
    .clk(and_1_out), .load(and_1_out), .clr(button_1_out), .d0(shift_register_6_q7[7]),
    .q0(shift_register_7_q7[7]), .d1(shift_register_6_q7[6]), .q1(shift_register_7_q7[6]),
    .d2(shift_register_6_q7[5]), .q2(shift_register_7_q7[5]), .d3(shift_register_6_q7[4]),
    .q3(shift_register_7_q7[4]), .d4(shift_register_6_q7[3]), .q4(shift_register_7_q7[3]),
    .d5(shift_register_6_q7[2]), .q5(shift_register_7_q7[2]), .d6(shift_register_6_q7[1]),
    .q6(shift_register_7_q7[1]), .d7(shift_register_6_q7[0]), .q7(shift_register_7_q7[0]));  // open: shift, in, out
  Shift_Register shift_register_8 (
    .clk(and_1_out), .load(and_1_out), .clr(button_1_out), .d0(shift_register_7_q7[7]),
    .q0(shift_register_8_q7[7]), .d1(shift_register_7_q7[6]), .q1(shift_register_8_q7[6]),
    .d2(shift_register_7_q7[5]), .q2(shift_register_8_q7[5]), .d3(shift_register_7_q7[4]),
    .q3(shift_register_8_q7[4]), .d4(shift_register_7_q7[3]), .q4(shift_register_8_q7[3]),
    .d5(shift_register_7_q7[2]), .q5(shift_register_8_q7[2]), .d6(shift_register_7_q7[1]),
    .q6(shift_register_8_q7[1]), .d7(shift_register_7_q7[0]), .q7(shift_register_8_q7[0]));  // open: shift, in, out
  or or_1 (or_1_out, and_4_out, and_5_out);
  or or_2 (or_2_out[0], shift_register_8_q7[0], decoder_2_out0[0]);
  Decoder #(.select(3)) decoder_2 (
    .out0(decoder_2_out0[0]), .out1(decoder_2_out0[1]), .out2(decoder_2_out0[2]), .out3(decoder_2_out0[3]),
    .out4(decoder_2_out0[4]), .out5(decoder_2_out0[5]), .out6(decoder_2_out0[6]), .out7(decoder_2_out0[7]),
    .sel(counter_1_q));  // open: en
  Counter #(.width(3), .max('h7)) counter_1 (
    .load(and_5_out), .count(or_1_out), .Q(counter_1_q), .clk(or_1_out));  // open: D, carry, clr
  or or_3 (or_2_out[1], shift_register_8_q7[1], decoder_2_out0[1]);
  or or_4 (or_2_out[2], shift_register_8_q7[2], decoder_2_out0[2]);
  or or_5 (or_2_out[3], shift_register_8_q7[3], decoder_2_out0[3]);
  or or_6 (or_2_out[4], shift_register_8_q7[4], decoder_2_out0[4]);
  or or_7 (or_2_out[5], shift_register_8_q7[5], decoder_2_out0[5]);
  or or_8 (or_2_out[6], shift_register_8_q7[6], decoder_2_out0[6]);
  or or_9 (or_2_out[7], shift_register_8_q7[7], decoder_2_out0[7]);
  Counter #(.width(4), .max('hf)) counter_2 (
    .count(and_2_out), .Q(counter_2_q), .clk(and_2_out), .clr(button_1_out));  // open: load, D, carry
  Comparator comparator_1 (.a(shift_register_8_q7), .b(decoder_2_out0), .eq(comparator_1_eq));  // open: gt, lt
  Counter #(.width(4), .max('hf)) counter_3 (
    .count(and_6_out), .Q(counter_3_q), .clk(and_6_out), .clr(or_10_out));  // open: load, D, carry
  or or_10 (or_10_out, button_1_out, and_2_out);
  and and_2 (and_2_out, counter_3_q[1], counter_3_q[3]);
  // AND_Gate and_3 has open pins: in0=counter_3_q[0], in1=counter_3_q[3], out=open
  DotMatrix #(.inputtype("row"), .matrixcols(8), .matrixrows(8)) dotmatrix_1 (
    .row0(shift_register_1_q7), .row1(shift_register_2_q7), .row2(shift_register_3_q7),
    .row3(shift_register_4_q7), .row4(shift_register_5_q7), .row5(shift_register_6_q7),
    .row6(shift_register_7_q7), .row7(or_2_out));
  Button R (.out(R_out));
  Button L (.out(L_out));
  Button button_1 (.out(button_1_out));
  and and_4 (and_4_out, not_2_out, L_out);
  Hex_Digit_Display hex_digit_display_1 (.value(counter_2_q));  // open: dp
  LED led_1 (.in(comparator_1_eq));
  Hex_Digit_Display hex_digit_display_2 (.value(shift_register_9_q0));  // open: dp
  not not_2 (not_2_out, comparator_1_eq);
  and and_5 (and_5_out, R_out, not_2_out);
  Counter #(.width(4), .max('hf)) counter_4 (
    .count(and_8_out), .Q(counter_4_q), .clk(and_8_out), .clr(or_11_out));  // open: load, D, carry
  or or_11 (or_11_out, button_1_out, and_6_out);
  and and_6 (and_6_out, counter_4_q[1], counter_4_q[3]);
  // AND_Gate and_7 has open pins: in0=counter_4_q[0], in1=counter_4_q[3], out=open
  Hex_Digit_Display hex_digit_display_3 (.value(counter_3_q));  // open: dp
  Hex_Digit_Display hex_digit_display_4 (.value(counter_4_q));  // open: dp
  Hex_Digit_Display hex_digit_display_5 (.value(shift_register_9_q2));  // open: dp
  Hex_Digit_Display hex_digit_display_6 (.value(shift_register_9_q1));  // open: dp
  Shift_Register #(.width(4), .length(4)) shift_register_9 (
    .shift(1'b0), .clk(comparator_1_eq), .load(comparator_2_gt), .d0(counter_2_q), .q0(shift_register_9_q0),
    .d1(counter_3_q), .q1(shift_register_9_q1), .d2(counter_4_q), .q2(shift_register_9_q2), .d3(counter_5_q),
    .q3(shift_register_9_q3));  // open: in, out, clr
  Counter #(.width(4), .max('hf)) counter_5 (
    .Q(counter_5_q), .clk(and_1_out), .clr(or_12_out));  // open: load, D, count, carry
  or or_12 (or_12_out, button_1_out, and_8_out);
  and and_8 (and_8_out, counter_5_q[1], counter_5_q[3]);
  // AND_Gate and_9 has open pins: in0=counter_5_q[0], in1=counter_5_q[3], out=open
  Hex_Digit_Display hex_digit_display_7 (.value(counter_5_q));  // open: dp
  Hex_Digit_Display hex_digit_display_8 (.value(shift_register_9_q3));  // open: dp
  Comparator #(.width(16)) comparator_2 (
    .a({counter_2_q, counter_3_q, counter_4_q, counter_5_q}),
    .b({shift_register_9_q0, shift_register_9_q1, shift_register_9_q2, shift_register_9_q3}),
    .gt(comparator_2_gt));  // open: eq, lt

  // Notes on the sheet:
  //   Current Score
  //   High Score
endmodule
