// Logisim project player_controls.circ as structural Verilog: 1 circuit, main circuit main
// 8
module main (
);

  wire button_1_out, button_2_out, or_1_out, or_2_out;
  wire [2:0] counter_1_q;
  wire [7:0] decoder_1_out0;

  Decoder #(.select(3)) decoder_1 (
    .out0(decoder_1_out0[0]), .out1(decoder_1_out0[1]), .out2(decoder_1_out0[2]), .out3(decoder_1_out0[3]),
    .out4(decoder_1_out0[4]), .out5(decoder_1_out0[5]), .out6(decoder_1_out0[6]), .out7(decoder_1_out0[7]),
    .sel(counter_1_q));  // open: en
  Counter #(.width(3), .max('h7)) counter_1 (
    .load(button_2_out), .count(or_1_out), .Q(counter_1_q), .clk(or_2_out));  // open: D, carry, clr
  or or_1 (or_1_out, button_2_out, button_1_out);
  or or_2 (or_2_out, button_2_out, button_1_out);
  Button button_1 (.out(button_1_out));
  Button button_2 (.out(button_2_out));
  DotMatrix #(.inputtype("row"), .matrixcols(8), .matrixrows(8)) dotmatrix_1 (.row7(decoder_1_out0));  // open: row0, row1, row2, row3, row4, row5, row6
endmodule
